// Logisim project Real_Alu-Gabri-salvo.circ as structural Verilog
module A_And_B (
  input  [7:0] A,
  input  [7:0] B,
  output [7:0] out_3
);

  assign out_3 = A & B;  // AND_Gate and_1, 8 bits wide
endmodule

module in_A_OR_in_B (
  input  [7:0] A,
  input  [7:0] B,
  output [7:0] out_3
);

  assign out_3 = A | B;  // OR_Gate or_1, 8 bits wide
endmodule

module Full_adder (
  input  C0,
  input  a,
  input  b,
  output S,
  output C1
);

  wire and_1_out, and_2_out, and_3_out, xor_1_out;

  xor xor_1 (xor_1_out, a, b);
  and and_1 (and_1_out, C0, a);
  and and_2 (and_2_out, a, b);
  and and_3 (and_3_out, C0, b);
  xor xor_2 (S, xor_1_out, C0);
  or or_1 (C1, and_1_out, and_2_out, and_3_out);
endmodule

module adder_4_bit (
  input  c0,
  input  a0,
  input  b0,
  input  a1,
  input  b1,
  input  a2,
  input  b2,
  input  a3,
  input  b3,
  output s0,
  output s1,
  output s2,
  output s3,
  output C
);

  wire full_adder_1_c1, full_adder_2_c1, full_adder_3_c1;

  Full_adder full_adder_1 (.S(s0), .C1(full_adder_1_c1), .C0(c0), .a(a0), .b(b0));
  Full_adder full_adder_2 (.S(s1), .C1(full_adder_2_c1), .C0(full_adder_1_c1), .a(a1), .b(b1));
  Full_adder full_adder_3 (.S(s2), .C1(full_adder_3_c1), .C0(full_adder_2_c1), .a(a2), .b(b2));
  Full_adder full_adder_4 (.S(s3), .C1(C), .C0(full_adder_3_c1), .a(a3), .b(b3));
endmodule
